// Logisim project MIPS.circ as structural Verilog: 3 circuits, main circuit MIPS
module MIPS (
  input  in_1,
  input  in_2,
  output [3:0] Rs,
  output [3:0] Rt,
  output [3:0] Rd,
  output [3:0] DestReg,
  output [7:0] t4,
  output [7:0] t3,
  output [7:0] t2,
  output [7:0] t1,
  output [7:0] t0,
  output [7:0] sp,
  output [7:0] A,
  output [7:0] B,
  output [7:0] Res_Address,
  output [7:0] WriteData
);

  wire alu_1_zero_flag, clock_1_out, control_unit_1_alusrc, control_unit_1_beq, control_unit_1_bneq,
       control_unit_1_jump, control_unit_1_memread, control_unit_1_memtoreg, control_unit_1_memwrite,
       control_unit_1_regdst, control_unit_1_regwrite, multiplexer_4_out, shiftchecker_1_isshift;
  wire [2:0] control_unit_1_aluop;
  wire [3:0] instruction_memory_1_opcode, instruction_memory_1_shft_amnt;
  wire [7:0] adder_1_out, adder_2_out, data_memory_1_data_read, instruction_memory_1_addrss_imm,
       instruction_memory_1_jmpaddr, instruction_memory_1_pc_read, multiplexer_1_out, multiplexer_3_out,
       multiplexer_5_out, multiplexer_6_out, multiplexer_8_out, n4to8bit_1_out;

  Clock clock_1 (.out(clock_1_out));
  Multiplexer #(.width(8), .enable("false")) multiplexer_1 (
    .in0({8{1'b0}}), .in1(multiplexer_5_out), .out(multiplexer_1_out), .sel(in_1));
  // Probe on multiplexer_5_out
  Adder adder_1 (.a(instruction_memory_1_pc_read), .b(8'h1), .out(adder_1_out));  // open: cin, cout
  Instruction_Memory instruction_memory_1 (
    .PC_write(multiplexer_1_out), .Clk(clock_1_out), .Reset(in_2), .PC_Read(instruction_memory_1_pc_read),
    .Opcode(instruction_memory_1_opcode), .Src_1(Rs), .Src_2(Rt), .Dst_reg(Rd),
    .Shft_amnt(instruction_memory_1_shft_amnt), .JmpAddr(instruction_memory_1_jmpaddr),
    .Addrss_imm(instruction_memory_1_addrss_imm));
  _4to8bit u_4to8bit_1 (.in(instruction_memory_1_shft_amnt), .out(n4to8bit_1_out));
  Adder adder_2 (.a(instruction_memory_1_addrss_imm), .b(adder_1_out), .out(adder_2_out));  // open: cin, cout
  Multiplexer #(.width(4), .enable("false")) multiplexer_2 (
    .in0(Rt), .in1(Rd), .out(DestReg), .sel(control_unit_1_regdst));
  Control_Unit control_unit_1 (
    .OP_code(instruction_memory_1_opcode), .ALUop(control_unit_1_aluop), .jump(control_unit_1_jump),
    .bneq(control_unit_1_bneq), .beq(control_unit_1_beq), .MemWrite(control_unit_1_memwrite),
    .MemRead(control_unit_1_memread), .RegWrite(control_unit_1_regwrite), .MemToReg(control_unit_1_memtoreg),
    .ALUsrc(control_unit_1_alusrc), .RegDst(control_unit_1_regdst));
  Multiplexer #(.width(8), .enable("false")) multiplexer_3 (
    .in0(adder_1_out), .in1(adder_2_out), .out(multiplexer_3_out), .sel(multiplexer_4_out));
  Multiplexer #(.enable("false")) multiplexer_4 (
    .in0(control_unit_1_bneq), .in1(control_unit_1_beq), .out(multiplexer_4_out), .sel(alu_1_zero_flag));
  Register_File register_file_1 (
    .Dst_Reg_1(DestReg), .WriteData(multiplexer_8_out), .CLR(in_2), .SrcReg1(Rs), .SrcReg2(Rt),
    .RegWrite(control_unit_1_regwrite), .CLK(clock_1_out), .t3__t2__t1__t0_MSB__LSB({t3, t2, t1, t0}),
    .t4(t4), .Read_Data_1(A), .Read_Data_2(WriteData), .sp(sp));
  Multiplexer #(.width(8), .enable("false")) multiplexer_5 (
    .in0(multiplexer_3_out), .in1(instruction_memory_1_jmpaddr), .out(multiplexer_5_out),
    .sel(control_unit_1_jump));
  ShiftChecker shiftchecker_1 (.ALUop(control_unit_1_aluop), .isShift(shiftchecker_1_isshift));
  Multiplexer #(.width(8), .enable("false")) multiplexer_6 (
    .in0(instruction_memory_1_addrss_imm), .in1(n4to8bit_1_out), .out(multiplexer_6_out),
    .sel(shiftchecker_1_isshift));
  // Probe on multiplexer_6_out
  Multiplexer #(.width(8), .enable("false")) multiplexer_7 (
    .in0(WriteData), .in1(multiplexer_6_out), .out(B), .sel(control_unit_1_alusrc));
  ALU alu_1 (.A(A), .ALUop(control_unit_1_aluop), .B(B), .\output (Res_Address), .zero_flag(alu_1_zero_flag));
  Multiplexer #(.width(8), .enable("false")) multiplexer_8 (
    .in0(Res_Address), .in1(data_memory_1_data_read), .out(multiplexer_8_out), .sel(control_unit_1_memtoreg));
  Data_Memory data_memory_1 (
    .Address(Res_Address), .Write_Data(WriteData), .Clk(clock_1_out), .Data_Read(data_memory_1_data_read),
    .MemRead(control_unit_1_memread), .MemWrite(control_unit_1_memwrite), .Clear(in_2));
  // Probe on data_memory_1_data_read
endmodule

// SC
module ShiftChecker (
  input  [2:0] ALUop,
  output isShift
);

  wire and_1_out, and_2_out, not_1_out, not_2_out;

  not not_1 (not_1_out, ALUop[0]);
  not not_2 (not_2_out, ALUop[1]);
  and and_1 (and_1_out, not_1_out, ALUop[1], ALUop[2]);
  and and_2 (and_2_out, ALUop[0], not_2_out, ALUop[2]);
  or or_1 (isShift, and_1_out, and_2_out);

  // Notes on the sheet:
  //   sll 101 // srl 110
endmodule

// 4T8
module _4to8bit (
  input  [3:0] in,
  output [7:0] out
);


  assign out = {4'b0000, in};
endmodule
