// Logisim project control_unit.circ as structural Verilog: 2 circuits, main circuit Control Unit
module Control_Unit (
  input  [3:0] OP_code,
  output [2:0] ALUop,
  output jump,
  output bneq,
  output beq,
  output MemWrite,
  output MemRead,
  output RegWrite,
  output MemToReg,
  output ALUsrc,
  output RegDst
);

  ROM #(.addrWidth(4), .dataWidth(12)) rom_1 (
    .addr(OP_code), .data({RegDst, ALUsrc, MemToReg, RegWrite, MemRead, MemWrite, beq, bneq, jump, ALUop}));  // open: sel

  // Notes on the sheet:
  //   contents of rom_1 (hex, n*v repeats v):
  //   902 903 500 11 904 440 901 506 502 900 505 8 780 501 21 503
endmodule

module PipelineControlUnit (
  input  [3:0] OP_code,
  output [11:0] Controls
);

  ROM #(.addrWidth(4), .dataWidth(12)) rom_1 (.addr(OP_code), .data(Controls));  // open: sel

  // Notes on the sheet:
  //   contents of rom_1 (hex, n*v repeats v):
  //   902 903 500 11 904 440 901 906 502 900 905 8 780 501 21 503
endmodule
