// Logisim project data_mem.circ as structural Verilog: 1 circuit, main circuit Data Memory
module Data_Memory (
  input  MemRead,
  input  MemWrite,
  input  [7:0] Address,
  input  [7:0] Write_Data,
  input  Clk,
  input  Clear,
  output [7:0] Data_Read
);

  wire not_1_out;

  not not_1 (not_1_out, Clk);
  RAM #(.bus("separate")) ram_1 (
    .addr(Address), .din(Write_Data), .data(Data_Read), .str(MemWrite), .clk(not_1_out), .ld(MemRead),
    .clr(Clear));  // open: sel
endmodule
