// Logisim project instruction_mem.circ as structural Verilog: 1 circuit, main circuit Instruction Memory
module Instruction_Memory (
  input  [7:0] PC_write,
  input  Clk,
  input  Reset,
  output [7:0] PC_Read,
  output [3:0] Opcode,
  output [3:0] Src_1,
  output [3:0] Src_2,
  output [3:0] Dst_reg,
  output [3:0] Shft_amnt,
  output [7:0] JmpAddr,
  output [7:0] Addrss_imm
);

  Register #(.trigger("falling")) PC (.D(PC_write), .Q(PC_Read), .clk(Clk), .clr(Reset));  // open: en
  ROM #(.dataWidth(20)) rom_1 (.addr(PC_Read), .data({Opcode, JmpAddr, Addrss_imm}), .sel(1'b1));

  assign Dst_reg = Addrss_imm[7:4];
  assign Shft_amnt = Addrss_imm[3:0];
  assign Src_1 = JmpAddr[7:4];
  assign Src_2 = JmpAddr[3:0];

  // Notes on the sheet:
  //   contents of rom_1 (hex, n*v repeats v):
  //   2070a 20101 e710b 20102 e7109 20101 20201 20402 91230 90210 90320 24401 347fb b0f00 20301 56300
  //   d6601 73704 56700 d6601 a7405 56400 d6601 544a2 56400 d6601 c41a2 56100 d6601 21288 56200 d6601
  //   d2381 63230 56300 d6601 20746 20155 7120 56200 d6601 823fe 56300 d6601 20380 204aa 13410 56100 d6601
  //   f12ff 56200 d6601 b3400
endmodule
