// Logisim project register_file.circ as structural Verilog: 1 circuit, main circuit Register File
module Register_File (
  input  RegWrite,
  input  CLK,
  input  [3:0] Dst_Reg_1,
  input  [7:0] WriteData,
  input  CLR,
  input  [3:0] SrcReg1,
  input  [3:0] SrcReg2,
  output [31:0] t3__t2__t1__t0_MSB__LSB,
  output [7:0] t4,
  output [7:0] sp,
  output [7:0] Read_Data_1,
  output [7:0] Read_Data_2
);

  wire and_1_out, demultiplexer_1_out1, demultiplexer_1_out2, demultiplexer_1_out3, demultiplexer_1_out4,
       demultiplexer_1_out6, demultiplexer_1_out7, nor_1_out, not_1_out, not_2_out, not_3_out, not_4_out,
       not_5_out;
  wire [7:0] multiplexer_3_out;

  not not_1 (not_1_out, demultiplexer_1_out1);
  Register t1 (.D(WriteData), .Q(t3__t2__t1__t0_MSB__LSB[15:8]), .clk(not_1_out), .clr(CLR));  // open: en
  not not_2 (not_2_out, demultiplexer_1_out2);
  Register t2 (.D(WriteData), .Q(t3__t2__t1__t0_MSB__LSB[23:16]), .clk(not_2_out), .clr(CLR));  // open: en
  Multiplexer #(.select(3), .width(8), .enable("false")) multiplexer_1 (
    .in0({8{1'b0}}), .in1(t3__t2__t1__t0_MSB__LSB[15:8]), .in2(t3__t2__t1__t0_MSB__LSB[23:16]),
    .in3(t3__t2__t1__t0_MSB__LSB[31:24]), .in4(t4), .in5({8{1'b0}}), .in6(sp),
    .in7(t3__t2__t1__t0_MSB__LSB[7:0]), .out(Read_Data_1), .sel(SrcReg1[2:0]));
  Demultiplexer #(.select(3), .enable("false")) demultiplexer_1 (
    .out1(demultiplexer_1_out1), .out2(demultiplexer_1_out2), .out3(demultiplexer_1_out3),
    .out4(demultiplexer_1_out4), .out6(demultiplexer_1_out6), .out7(demultiplexer_1_out7), .in(and_1_out),
    .sel(Dst_Reg_1[2:0]));  // open: out0, out5
  not not_3 (not_3_out, demultiplexer_1_out3);
  Register t3 (.D(WriteData), .Q(t3__t2__t1__t0_MSB__LSB[31:24]), .clk(not_3_out), .clr(CLR));  // open: en
  and and_1 (and_1_out, RegWrite, CLK);
  not not_4 (not_4_out, demultiplexer_1_out4);
  Register u_t4 (.D(WriteData), .Q(t4), .clk(not_4_out), .clr(CLR));  // open: en
  Multiplexer #(.select(3), .width(8), .enable("false")) multiplexer_2 (
    .in0({8{1'b0}}), .in1(t3__t2__t1__t0_MSB__LSB[15:8]), .in2(t3__t2__t1__t0_MSB__LSB[23:16]),
    .in3(t3__t2__t1__t0_MSB__LSB[31:24]), .in4(t4), .in5({8{1'b0}}), .in6(sp),
    .in7(t3__t2__t1__t0_MSB__LSB[7:0]), .out(Read_Data_2), .sel(SrcReg2[2:0]));
  not not_5 (not_5_out, demultiplexer_1_out7);
  Register t0 (.D(WriteData), .Q(t3__t2__t1__t0_MSB__LSB[7:0]), .clk(not_5_out), .clr(CLR));  // open: en
  Multiplexer #(.width(8), .enable("false")) multiplexer_3 (
    .in0(WriteData), .in1({8{1'b1}}), .out(multiplexer_3_out), .sel(CLR));
  nor nor_1 (nor_1_out, demultiplexer_1_out6, CLR);
  Register u_sp (.D(multiplexer_3_out), .Q(sp), .clk(nor_1_out), .clr(1'b0));  // open: en

  // Notes on the sheet:
  //   $zero
endmodule
